// Logisim project minha-ula.circ as structural Verilog: 35 circuits, main circuit mux2
module mux2 (
  input  I0,
  input  I1,
  input  Sel,
  output out_4
);

  wire and_1_out, and_2_out;

  and and_1 (and_1_out, I0, ~Sel);  // AND_Gate
  and and_2 (and_2_out, I1, Sel);
  or or_1 (out_4, and_1_out, and_2_out);
endmodule

module mux2_4bits (
  input  [3:0] I0,
  input  [3:0] I1,
  input  in_3,
  output [3:0] out_4
);

  wire [3:0] and_1_out, and_2_out;

  assign and_1_out = I0 & ~{4{in_3}};  // AND_Gate and_1, 4 bits wide
  assign and_2_out = I1 & {4{in_3}};  // AND_Gate and_2, 4 bits wide
  assign out_4 = and_1_out | and_2_out;  // OR_Gate or_1, 4 bits wide
endmodule

module mux2_32bits (
  input  [31:0] I0,
  input  [31:0] I1,
  input  in_3,
  output [31:0] out_4
);

  wire [31:0] and_1_out, and_2_out;

  assign and_1_out = I0 & ~{32{in_3}};  // AND_Gate and_1, 32 bits wide
  assign and_2_out = I1 & {32{in_3}};  // AND_Gate and_2, 32 bits wide
  assign out_4 = and_1_out | and_2_out;  // OR_Gate or_1, 32 bits wide
endmodule

module mux4 (
  input  l0,
  input  l1,
  input  l2,
  input  l3,
  input  sel1,
  input  sel0,
  output out_7
);

  wire mux2_1_out_4, mux2_2_out_4;

  mux2 mux2_1 (.I0(l0), .I1(l1), .Sel(sel0), .out_4(mux2_1_out_4));
  mux2 mux2_2 (.I0(l2), .I1(l3), .Sel(sel0), .out_4(mux2_2_out_4));
  mux2 mux2_3 (.I0(mux2_1_out_4), .I1(mux2_2_out_4), .Sel(sel1), .out_4(out_7));
endmodule

module mux4b (
  input  l0,
  input  l1,
  input  l2,
  input  l3,
  input  [1:0] in_5,
  output out_6
);

  wire mux2_1_out_4, mux2_2_out_4;

  mux2 mux2_1 (.I0(l0), .I1(l1), .Sel(in_5[0]), .out_4(mux2_1_out_4));
  mux2 mux2_2 (.I0(l2), .I1(l3), .Sel(in_5[0]), .out_4(mux2_2_out_4));
  mux2 mux2_3 (.I0(mux2_1_out_4), .I1(mux2_2_out_4), .Sel(in_5[1]), .out_4(out_6));
endmodule

module mux8 (
  input  l0,
  input  l1,
  input  l2,
  input  l3,
  input  l4,
  input  l5,
  input  l6,
  input  l7,
  input  sel2,
  input  sel1,
  input  sel0,
  output out_12
);

  wire mux4_1_out_7, mux4_2_out_7;

  mux4 mux4_1 (.l0(l0), .l1(l1), .l2(l2), .l3(l3), .sel1(sel1), .sel0(sel0), .out_7(mux4_1_out_7));
  mux4 mux4_2 (.l0(l4), .l1(l5), .l2(l6), .l3(l7), .sel1(sel1), .sel0(sel0), .out_7(mux4_2_out_7));
  mux2 mux2_1 (.I0(mux4_1_out_7), .I1(mux4_2_out_7), .Sel(sel2), .out_4(out_12));
endmodule

module mux8b (
  input  l0,
  input  l1,
  input  l2,
  input  l3,
  input  l4,
  input  l5,
  input  l6,
  input  l7,
  input  [2:0] sel,
  output out_10
);

  wire mux4_1_out_7, mux4_2_out_7;

  mux4 mux4_1 (.l0(l0), .l1(l1), .l2(l2), .l3(l3), .sel1(sel[1]), .sel0(sel[0]), .out_7(mux4_1_out_7));
  mux4 mux4_2 (.l0(l4), .l1(l5), .l2(l6), .l3(l7), .sel1(sel[1]), .sel0(sel[0]), .out_7(mux4_2_out_7));
  mux2 mux2_1 (.I0(mux4_1_out_7), .I1(mux4_2_out_7), .Sel(sel[2]), .out_4(out_10));
endmodule

module mux16 (
  input  l0,
  input  l1,
  input  l2,
  input  l3,
  input  l4,
  input  l5,
  input  l6,
  input  l7,
  input  l8,
  input  l9,
  input  l10,
  input  l11,
  input  l12,
  input  l13,
  input  l14,
  input  l15,
  input  sel3,
  input  sel2,
  input  sel1,
  input  sel0,
  output out_21
);

  wire mux8_1_out_12, mux8_2_out_12;

  mux8 mux8_1 (
    .l0(l0), .l1(l1), .l2(l2), .l3(l3), .l4(l4), .l5(l5), .l6(l6), .l7(l7), .sel2(sel2), .sel1(sel1),
    .sel0(sel0), .out_12(mux8_1_out_12));
  mux8 mux8_2 (
    .l0(l8), .l1(l9), .l2(l10), .l3(l11), .l4(l12), .l5(l13), .l6(l14), .l7(l15), .sel2(sel2), .sel1(sel1),
    .sel0(sel0), .out_12(mux8_2_out_12));
  mux2 mux2_1 (.I0(mux8_1_out_12), .I1(mux8_2_out_12), .Sel(sel3), .out_4(out_21));
endmodule

module mux16b (
  input  l0,
  input  l1,
  input  l2,
  input  l3,
  input  l4,
  input  l5,
  input  l6,
  input  l7,
  input  l8,
  input  l9,
  input  l10,
  input  l11,
  input  l12,
  input  l13,
  input  l14,
  input  l15,
  input  [3:0] in_17,
  output out_18
);

  wire mux8_1_out_12, mux8_2_out_12;

  mux8 mux8_1 (
    .l0(l0), .l1(l1), .l2(l2), .l3(l3), .l4(l4), .l5(l5), .l6(l6), .l7(l7), .sel2(in_17[2]), .sel1(in_17[1]),
    .sel0(in_17[0]), .out_12(mux8_1_out_12));
  mux8 mux8_2 (
    .l0(l8), .l1(l9), .l2(l10), .l3(l11), .l4(l12), .l5(l13), .l6(l14), .l7(l15), .sel2(in_17[2]),
    .sel1(in_17[1]), .sel0(in_17[0]), .out_12(mux8_2_out_12));
  mux2 mux2_1 (.I0(mux8_1_out_12), .I1(mux8_2_out_12), .Sel(in_17[3]), .out_4(out_18));
endmodule

module mux32 (
  input  l0,
  input  l1,
  input  l2,
  input  l3,
  input  l4,
  input  l5,
  input  l6,
  input  l7,
  input  l8,
  input  l9,
  input  l10,
  input  l11,
  input  l12,
  input  l13,
  input  l14,
  input  l15,
  input  l16,
  input  l17,
  input  l18,
  input  l19,
  input  l20,
  input  l21,
  input  l22,
  input  l23,
  input  l24,
  input  l25,
  input  l26,
  input  l27,
  input  l28,
  input  l29,
  input  l30,
  input  sel5,
  input  sel3,
  input  sel2,
  input  sel1,
  input  sel0,
  input  l31,
  output out_38
);

  wire mux16_1_out_21, mux16_2_out_21;

  mux16 mux16_1 (
    .l0(l0), .l1(l1), .l2(l2), .l3(l3), .l4(l4), .l5(l5), .l6(l6), .l7(l7), .l8(l8), .l9(l9), .l10(l10),
    .l11(l11), .l12(l12), .l13(l13), .l14(l14), .l15(l15), .sel3(sel3), .sel2(sel2), .sel1(sel1),
    .sel0(sel0), .out_21(mux16_1_out_21));
  mux16 mux16_2 (
    .l0(l16), .l1(l17), .l2(l18), .l3(l19), .l4(l20), .l5(l21), .l6(l22), .l7(l23), .l8(l24), .l9(l25),
    .l10(l26), .l11(l27), .l12(l28), .l13(l29), .l14(l30), .l15(l31), .sel3(sel3), .sel2(sel2), .sel1(sel1),
    .sel0(sel0), .out_21(mux16_2_out_21));
  mux2 mux2_1 (.I0(mux16_1_out_21), .I1(mux16_2_out_21), .Sel(sel5), .out_4(out_38));
endmodule

module mux32b (
  input  l0,
  input  l1,
  input  l2,
  input  l3,
  input  l4,
  input  l5,
  input  l6,
  input  l7,
  input  l8,
  input  l9,
  input  l10,
  input  l11,
  input  l12,
  input  l13,
  input  l14,
  input  l15,
  input  l16,
  input  l17,
  input  l18,
  input  l19,
  input  l20,
  input  l21,
  input  l22,
  input  l23,
  input  l24,
  input  l25,
  input  l26,
  input  l27,
  input  l28,
  input  l29,
  input  l30,
  input  l31,
  input  [4:0] in_33,
  output out_34
);

  wire mux16_1_out_21, mux16_2_out_21;

  mux16 mux16_1 (
    .l0(l0), .l1(l1), .l2(l2), .l3(l3), .l4(l4), .l5(l5), .l6(l6), .l7(l7), .l8(l8), .l9(l9), .l10(l10),
    .l11(l11), .l12(l12), .l13(l13), .l14(l14), .l15(l15), .sel3(in_33[3]), .sel2(in_33[2]), .sel1(in_33[1]),
    .sel0(in_33[0]), .out_21(mux16_1_out_21));
  mux16 mux16_2 (
    .l0(l16), .l1(l17), .l2(l18), .l3(l19), .l4(l20), .l5(l21), .l6(l22), .l7(l23), .l8(l24), .l9(l25),
    .l10(l26), .l11(l27), .l12(l28), .l13(l29), .l14(l30), .l15(l31), .sel3(in_33[3]), .sel2(in_33[2]),
    .sel1(in_33[1]), .sel0(in_33[0]), .out_21(mux16_2_out_21));
  mux2 mux2_1 (.I0(mux16_1_out_21), .I1(mux16_2_out_21), .Sel(in_33[4]), .out_4(out_34));
endmodule

module somador (
  input  vem1,
  input  B,
  input  A,
  output soma,
  output vai1
);

  wire and_1_out, and_2_out, and_3_out, and_4_out, or_1_out, xnor_1_out, xor_1_out;

  xor xor_1 (xor_1_out, B, A);
  or or_1 (or_1_out, B, A);
  xnor xnor_1 (xnor_1_out, B, A);
  and and_1 (and_1_out, B, A);
  and and_2 (and_2_out, or_1_out, vem1);
  and and_3 (and_3_out, xnor_1_out, vem1);
  and and_4 (and_4_out, xor_1_out, ~vem1);  // AND_Gate
  or or_2 (vai1, and_1_out, and_2_out);
  or or_3 (soma, and_3_out, and_4_out);
endmodule

module ShiftLeftLogical (
  input  [3:0] in_1,
  input  shift,
  output [3:0] out_3
);

  mux2_4bits mux2_4bits_1 (.I0(in_1), .I1({in_1[2:0], 1'b0}), .in_3(shift), .out_4(out_3));

  // Notes on the sheet:
  //   Deslocar para esquerda é o mesmo que multiplicar por 2
endmodule

module ShiftRightLogical (
  input  [3:0] in_1,
  input  in_2,
  output [3:0] out_3
);

  mux2_4bits mux2_4bits_1 (.I0(in_1), .I1({1'b0, in_1[3:1]}), .in_3(in_2), .out_4(out_3));

  // Notes on the sheet:
  //   Deslocar para direita é o mesmo que dividir por 2
endmodule

module ShiftLeftArith (
  input  [3:0] in_1,
  input  in_2,
  output [3:0] out_3
);

  mux2_4bits mux2_4bits_1 (.I0(in_1), .I1({in_1[2:0], in_1[0]}), .in_3(in_2), .out_4(out_3));
endmodule

module ShiftRightArith (
  input  [3:0] in_1,
  input  in_2,
  output [3:0] out_3
);

  mux2_4bits mux2_4bits_1 (.I0(in_1), .I1({{2{in_1[3]}}, in_1[2:1]}), .in_3(in_2), .out_4(out_3));
endmodule

module UlaCell (
  input  a,
  input  b,
  input  vem1,
  input  [4:0] OpCode,
  output saida,
  output vai1
);

  wire and_1_out, nand_1_out, or_1_out, somador_1_soma, xor_1_out;

  and and_1 (and_1_out, b, a);
  or or_1 (or_1_out, b, a);
  somador somador_1 (.B(b), .A(a), .vem1(vem1), .vai1(vai1), .soma(somador_1_soma));
  xor xor_1 (xor_1_out, b, a);
  nand nand_1 (nand_1_out, ~a, b);  // NAND_Gate
  mux32b mux32b_1 (
    .l0(and_1_out), .l1(or_1_out), .l2(somador_1_soma), .l3(xor_1_out), .l4(a), .l5(b), .l6(a), .l7(b),
    .l8(a), .l9(b), .l10(a), .l11(b), .l31(nand_1_out), .in_33(OpCode), .out_34(saida));  // open: l12, l13, l14, l15, l16, l17, l18, l19, l20, l21, l22, l23, l24, l25, l26, l27, l28, l29, l30

  // Notes on the sheet:
  //   00001 - OR
  //   00000 - AND
  //   00010 - SOMADOR
  //   00011 - XOR
  //   00100 - SLL A
  //   00101 - SLL B
  //   00110 - SRL A
  //   00111 - SRL B
  //   01000 - SLA A
  //   01001 - SLA B
  //   01010 - SRA A
  //   01011 - SRA B
endmodule

module SLLADetector (
  input  [4:0] UlaOpCode,
  output out_2
);

  and and_1 (out_2, ~UlaOpCode[0], ~UlaOpCode[1], UlaOpCode[2], ~UlaOpCode[3], ~UlaOpCode[4]);  // AND_Gate
endmodule

module SLLBDetector (
  input  [4:0] UlaOpCode,
  output saida
);

  and and_1 (saida, ~UlaOpCode[4], ~UlaOpCode[3], UlaOpCode[2], ~UlaOpCode[1], UlaOpCode[0]);  // AND_Gate
endmodule

module SRLADetector (
  input  [4:0] UlaOpCode,
  output out_2
);

  and and_1 (out_2, ~UlaOpCode[0], UlaOpCode[1], UlaOpCode[2], ~UlaOpCode[3], ~UlaOpCode[4]);  // AND_Gate
endmodule

module SRLBDetector (
  input  [4:0] UlaOpCode,
  output out_2
);

  and and_1 (out_2, ~UlaOpCode[4], ~UlaOpCode[3], UlaOpCode[2], UlaOpCode[1], UlaOpCode[0]);  // AND_Gate
endmodule

module SLAADetector (
  input  [4:0] UlaOpCode,
  output out_2
);

  and and_1 (out_2, ~UlaOpCode[4], UlaOpCode[3], ~UlaOpCode[2], ~UlaOpCode[1], ~UlaOpCode[0]);  // AND_Gate
endmodule

module SLABDetector (
  input  [4:0] UlaOpCode,
  output out_2
);

  and and_1 (out_2, ~UlaOpCode[4], UlaOpCode[3], ~UlaOpCode[2], ~UlaOpCode[1], UlaOpCode[0]);  // AND_Gate
endmodule

module SRAADetector (
  input  [4:0] UlaOpCode,
  output out_2
);

  and and_1 (out_2, ~UlaOpCode[4], UlaOpCode[3], ~UlaOpCode[2], UlaOpCode[1], ~UlaOpCode[0]);  // AND_Gate
endmodule

module SRABDetector (
  input  [4:0] UlaOpCode,
  output out_2
);

  and and_1 (out_2, ~UlaOpCode[4], UlaOpCode[3], ~UlaOpCode[2], UlaOpCode[1], UlaOpCode[0]);  // AND_Gate
endmodule

module ULA (
  input  [3:0] A,
  input  [3:0] B,
  input  [4:0] UlaOpCode,
  output [3:0] out_4
);

  wire slladetector_1_out_2, sllbdetector_1_saida, ulacell_2_vai1, ulacell_3_vai1, ulacell_4_vai1;
  wire [3:0] SLLA_out_3, SLLB_out_3;

  ShiftLeftLogical SLLA (.in_1(A), .shift(slladetector_1_out_2), .out_3(SLLA_out_3));
  SLLADetector slladetector_1 (.out_2(slladetector_1_out_2), .UlaOpCode(UlaOpCode));
  ShiftLeftLogical SLLB (.in_1(B), .shift(sllbdetector_1_saida), .out_3(SLLB_out_3));
  SLLBDetector sllbdetector_1 (.saida(sllbdetector_1_saida), .UlaOpCode(UlaOpCode));
  UlaCell ulacell_1 (
    .a(SLLA_out_3[3]), .b(SLLB_out_3[3]), .OpCode(UlaOpCode), .saida(out_4[3]), .vem1(ulacell_2_vai1));  // open: vai1
  UlaCell ulacell_2 (
    .vai1(ulacell_2_vai1), .a(SLLA_out_3[2]), .b(SLLB_out_3[2]), .OpCode(UlaOpCode), .saida(out_4[2]),
    .vem1(ulacell_4_vai1));
  UlaCell ulacell_3 (
    .vai1(ulacell_3_vai1), .a(SLLA_out_3[0]), .b(SLLB_out_3[0]), .OpCode(UlaOpCode), .saida(out_4[0]),
    .vem1(1'b0));
  UlaCell ulacell_4 (
    .vai1(ulacell_4_vai1), .a(SLLA_out_3[1]), .b(SLLB_out_3[1]), .OpCode(UlaOpCode), .saida(out_4[1]),
    .vem1(ulacell_3_vai1));

  // Notes on the sheet:
  //   00000 - AND
  //   00001 - OR
  //   00010 - SOMADOR
  //   00011 - XOR
  //   00100 - SLL A
  //   00101 - SLL B
  //   00110 - SRL A
  //   00111 - SRL B
endmodule

module ULA32bits (
  input  [31:0] A,
  input  [31:0] B,
  input  [4:0] ULAOpCode,
  output out_4,
  output [31:0] result,
  output Zero
);

  wire slaadetector_1_out_2, slabdetector_1_out_2, slladetector_1_out_2, sllbdetector_1_saida,
       sraadetector_1_out_2, srabdetector_1_out_2, srladetector_1_out_2, srlbdetector_1_out_2,
       ulacell_2_vai1, ulacell_3_vai1, ulacell_4_vai1, ulacell_5_vai1, ulacell_6_vai1, ulacell_7_vai1,
       ulacell_8_vai1, ulacell_9_vai1, ulacell_10_vai1, ulacell_11_vai1, ulacell_12_vai1, ulacell_13_vai1,
       ulacell_14_vai1, ulacell_15_vai1, ulacell_16_vai1, ulacell_17_vai1, ulacell_18_vai1, ulacell_19_vai1,
       ulacell_20_vai1, ulacell_21_vai1, ulacell_22_vai1, ulacell_23_vai1, ulacell_24_vai1, ulacell_25_vai1,
       ulacell_26_vai1, ulacell_27_vai1, ulacell_28_vai1, ulacell_29_vai1, ulacell_30_vai1, ulacell_31_vai1,
       ulacell_32_vai1;
  wire [31:0] SLAA_out_3, SLAB_out_3, SLLA_out_3, SLLB_out_3, SRAA_out_3, SRAB_out_3, SRLA_out_3, SRLB_out_3;

  SLL32bits SLLB (.in_1(B), .shift(sllbdetector_1_saida), .out_3(SLLB_out_3));
  SLLBDetector sllbdetector_1 (.saida(sllbdetector_1_saida), .UlaOpCode(ULAOpCode));
  SLL32bits SLLA (.in_1(A), .shift(slladetector_1_out_2), .out_3(SLLA_out_3));
  SLLADetector slladetector_1 (.out_2(slladetector_1_out_2), .UlaOpCode(ULAOpCode));
  SRL32bits SRLB (.in_1(SLLB_out_3), .shift(srlbdetector_1_out_2), .out_3(SRLB_out_3));
  SRLBDetector srlbdetector_1 (.out_2(srlbdetector_1_out_2), .UlaOpCode(ULAOpCode));
  SRL32bits SRLA (.in_1(SLLA_out_3), .shift(srladetector_1_out_2), .out_3(SRLA_out_3));
  SLAADetector slaadetector_1 (.out_2(slaadetector_1_out_2), .UlaOpCode(ULAOpCode));
  SRLADetector srladetector_1 (.out_2(srladetector_1_out_2), .UlaOpCode(ULAOpCode));
  and and_1 (Zero, ~result[31], ~result[30], ~result[29], ~result[28], ~result[27], ~result[26], ~result[25], ~result[24], ~result[23], ~result[22], ~result[21], ~result[20], ~result[19], ~result[18], ~result[17], ~result[16], ~result[15], ~result[14], ~result[13], ~result[12], ~result[11], ~result[10], ~result[9], ~result[8], ~result[7], ~result[6], ~result[5], ~result[4], ~result[3], ~result[2], ~result[1], ~result[0]);  // AND_Gate
  SLA32bits SLAB (.in_1(SRLB_out_3), .shift(slabdetector_1_out_2), .out_3(SLAB_out_3));
  SRABDetector srabdetector_1 (.out_2(srabdetector_1_out_2), .UlaOpCode(ULAOpCode));
  SLABDetector slabdetector_1 (.out_2(slabdetector_1_out_2), .UlaOpCode(ULAOpCode));
  SRA32bits SRAA (.in_1(SLAA_out_3), .shift(sraadetector_1_out_2), .out_3(SRAA_out_3));
  SLA32bits SLAA (.in_1(SRLA_out_3), .shift(slaadetector_1_out_2), .out_3(SLAA_out_3));
  SRAADetector sraadetector_1 (.out_2(sraadetector_1_out_2), .UlaOpCode(ULAOpCode));
  SRA32bits SRAB (.in_1(SLAB_out_3), .shift(srabdetector_1_out_2), .out_3(SRAB_out_3));
  UlaCell ulacell_1 (
    .vai1(out_4), .a(SRAA_out_3[31]), .b(SRAB_out_3[31]), .OpCode(ULAOpCode), .saida(result[31]),
    .vem1(ulacell_2_vai1));
  UlaCell ulacell_2 (
    .vai1(ulacell_2_vai1), .a(SRAA_out_3[30]), .b(SRAB_out_3[30]), .OpCode(ULAOpCode), .saida(result[30]),
    .vem1(ulacell_3_vai1));
  UlaCell ulacell_3 (
    .vai1(ulacell_3_vai1), .a(SRAA_out_3[29]), .b(SRAB_out_3[29]), .OpCode(ULAOpCode), .saida(result[29]),
    .vem1(ulacell_5_vai1));
  UlaCell ulacell_4 (
    .vai1(ulacell_4_vai1), .a(SRAA_out_3[27]), .b(SRAB_out_3[27]), .OpCode(ULAOpCode), .saida(result[27]),
    .vem1(ulacell_6_vai1));
  UlaCell ulacell_5 (
    .vai1(ulacell_5_vai1), .a(SRAA_out_3[28]), .b(SRAB_out_3[28]), .OpCode(ULAOpCode), .saida(result[28]),
    .vem1(ulacell_4_vai1));
  UlaCell ulacell_6 (
    .vai1(ulacell_6_vai1), .a(SRAA_out_3[26]), .b(SRAB_out_3[26]), .OpCode(ULAOpCode), .saida(result[26]),
    .vem1(ulacell_7_vai1));
  UlaCell ulacell_7 (
    .vai1(ulacell_7_vai1), .a(SRAA_out_3[25]), .b(SRAB_out_3[25]), .OpCode(ULAOpCode), .saida(result[25]),
    .vem1(ulacell_8_vai1));
  UlaCell ulacell_8 (
    .vai1(ulacell_8_vai1), .a(SRAA_out_3[24]), .b(SRAB_out_3[24]), .OpCode(ULAOpCode), .saida(result[24]),
    .vem1(ulacell_9_vai1));
  UlaCell ulacell_9 (
    .vai1(ulacell_9_vai1), .a(SRAA_out_3[23]), .b(SRAB_out_3[23]), .OpCode(ULAOpCode), .saida(result[23]),
    .vem1(ulacell_10_vai1));
  UlaCell ulacell_10 (
    .vai1(ulacell_10_vai1), .a(SRAA_out_3[22]), .b(SRAB_out_3[22]), .OpCode(ULAOpCode), .saida(result[22]),
    .vem1(ulacell_11_vai1));
  UlaCell ulacell_11 (
    .vai1(ulacell_11_vai1), .a(SRAA_out_3[21]), .b(SRAB_out_3[21]), .OpCode(ULAOpCode), .saida(result[21]),
    .vem1(ulacell_13_vai1));
  UlaCell ulacell_12 (
    .vai1(ulacell_12_vai1), .a(SRAA_out_3[19]), .b(SRAB_out_3[19]), .OpCode(ULAOpCode), .saida(result[19]),
    .vem1(ulacell_14_vai1));
  UlaCell ulacell_13 (
    .vai1(ulacell_13_vai1), .a(SRAA_out_3[20]), .b(SRAB_out_3[20]), .OpCode(ULAOpCode), .saida(result[20]),
    .vem1(ulacell_12_vai1));
  UlaCell ulacell_14 (
    .vai1(ulacell_14_vai1), .a(SRAA_out_3[18]), .b(SRAB_out_3[18]), .OpCode(ULAOpCode), .saida(result[18]),
    .vem1(ulacell_15_vai1));
  UlaCell ulacell_15 (
    .vai1(ulacell_15_vai1), .a(SRAA_out_3[17]), .b(SRAB_out_3[17]), .OpCode(ULAOpCode), .saida(result[17]),
    .vem1(ulacell_16_vai1));
  UlaCell ulacell_16 (
    .vai1(ulacell_16_vai1), .a(SRAA_out_3[16]), .b(SRAB_out_3[16]), .OpCode(ULAOpCode), .saida(result[16]),
    .vem1(ulacell_18_vai1));
  UlaCell ulacell_17 (
    .vai1(ulacell_17_vai1), .a(SRAA_out_3[14]), .b(SRAB_out_3[14]), .OpCode(ULAOpCode), .saida(result[14]),
    .vem1(ulacell_19_vai1));
  UlaCell ulacell_18 (
    .vai1(ulacell_18_vai1), .a(SRAA_out_3[15]), .b(SRAB_out_3[15]), .OpCode(ULAOpCode), .saida(result[15]),
    .vem1(ulacell_17_vai1));
  UlaCell ulacell_19 (
    .vai1(ulacell_19_vai1), .a(SRAA_out_3[13]), .b(SRAB_out_3[13]), .OpCode(ULAOpCode), .saida(result[13]),
    .vem1(ulacell_21_vai1));
  UlaCell ulacell_20 (
    .vai1(ulacell_20_vai1), .a(SRAA_out_3[11]), .b(SRAB_out_3[11]), .OpCode(ULAOpCode), .saida(result[11]),
    .vem1(ulacell_23_vai1));
  UlaCell ulacell_21 (
    .vai1(ulacell_21_vai1), .a(SRAA_out_3[12]), .b(SRAB_out_3[12]), .OpCode(ULAOpCode), .saida(result[12]),
    .vem1(ulacell_20_vai1));
  UlaCell ulacell_22 (
    .vai1(ulacell_22_vai1), .a(SRAA_out_3[9]), .b(SRAB_out_3[9]), .OpCode(ULAOpCode), .saida(result[9]),
    .vem1(ulacell_24_vai1));
  UlaCell ulacell_23 (
    .vai1(ulacell_23_vai1), .a(SRAA_out_3[10]), .b(SRAB_out_3[10]), .OpCode(ULAOpCode), .saida(result[10]),
    .vem1(ulacell_22_vai1));
  UlaCell ulacell_24 (
    .vai1(ulacell_24_vai1), .a(SRAA_out_3[8]), .b(SRAB_out_3[8]), .OpCode(ULAOpCode), .saida(result[8]),
    .vem1(ulacell_26_vai1));
  UlaCell ulacell_25 (
    .vai1(ulacell_25_vai1), .a(SRAA_out_3[6]), .b(SRAB_out_3[6]), .OpCode(ULAOpCode), .saida(result[6]),
    .vem1(ulacell_27_vai1));
  UlaCell ulacell_26 (
    .vai1(ulacell_26_vai1), .a(SRAA_out_3[7]), .b(SRAB_out_3[7]), .OpCode(ULAOpCode), .saida(result[7]),
    .vem1(ulacell_25_vai1));
  UlaCell ulacell_27 (
    .vai1(ulacell_27_vai1), .a(SRAA_out_3[5]), .b(SRAB_out_3[5]), .OpCode(ULAOpCode), .saida(result[5]),
    .vem1(ulacell_29_vai1));
  UlaCell ulacell_28 (
    .vai1(ulacell_28_vai1), .a(SRAA_out_3[3]), .b(SRAB_out_3[3]), .OpCode(ULAOpCode), .saida(result[3]),
    .vem1(ulacell_30_vai1));
  UlaCell ulacell_29 (
    .vai1(ulacell_29_vai1), .a(SRAA_out_3[4]), .b(SRAB_out_3[4]), .OpCode(ULAOpCode), .saida(result[4]),
    .vem1(ulacell_28_vai1));
  UlaCell ulacell_30 (
    .vai1(ulacell_30_vai1), .a(SRAA_out_3[2]), .b(SRAB_out_3[2]), .OpCode(ULAOpCode), .saida(result[2]),
    .vem1(ulacell_31_vai1));
  UlaCell ulacell_31 (
    .vai1(ulacell_31_vai1), .a(SRAA_out_3[1]), .b(SRAB_out_3[1]), .OpCode(ULAOpCode), .saida(result[1]),
    .vem1(ulacell_32_vai1));
  UlaCell ulacell_32 (
    .vai1(ulacell_32_vai1), .a(SRAA_out_3[0]), .b(SRAB_out_3[0]), .OpCode(ULAOpCode), .saida(result[0]),
    .vem1(1'b0));

  // Notes on the sheet:
  //   00000 - AND
  //   00001 - OR
  //   00011 - XOR
  //   00100 - SLL A
  //   00101 - SLL B
  //   00110 - SRL A
  //   00111 - SRL B
  //   01000 - SLA A
  //   01001 - SLA B
  //   01010 - SRA A
  //   01011 - SRA B
  //   00010 - SOMADOR
endmodule

module SLL32bits (
  input  [31:0] in_1,
  input  shift,
  output [31:0] out_3
);

  mux2_32bits mux2_32bits_1 (.I0(in_1), .I1({in_1[30:0], 1'b0}), .in_3(shift), .out_4(out_3));
endmodule

module SRL32bits (
  input  [31:0] in_1,
  input  shift,
  output [31:0] out_3
);

  mux2_32bits mux2_32bits_1 (.I0(in_1), .I1({1'b0, in_1[31:1]}), .in_3(shift), .out_4(out_3));
endmodule

module SLA32bits (
  input  [31:0] in_1,
  input  shift,
  output [31:0] out_3
);

  mux2_32bits mux2_32bits_1 (.I0(in_1), .I1({in_1[30:0], in_1[0]}), .in_3(shift), .out_4(out_3));
endmodule

module SRA32bits (
  input  [31:0] in_1,
  input  shift,
  output [31:0] out_3
);

  mux2_32bits mux2_32bits_1 (.I0(in_1), .I1({{2{in_1[31]}}, in_1[30:1]}), .in_3(shift), .out_4(out_3));
endmodule

module \final  (
  input  [31:0] A,
  input  [31:0] B,
  input  [4:0] ULAOpCode,
  output Resultado,
  output Zero,
  output [31:0] out_6
);

  ULA32bits ula32bits_1 (.ULAOpCode(ULAOpCode), .A(A), .B(B), .result(out_6), .out_4(Resultado), .Zero(Zero));

  // Notes on the sheet:
  //   00000 - AND
  //   00001 - OR
  //   00010 - SOMADOR
  //   00011 - XOR
  //   00100 - SLL A
  //   00101 - SLL B
  //   00110 - SRL A
  //   00111 - SRL B
  //   01000 - SLA A
  //   01001 - SLA B
  //   01010 - SRA A
  //   01011 - SRA B
endmodule

module flip_flop (
  input  [31:0] A,
  input  Save,
  input  Reset,
  output [31:0] out_4
);

  D_Flip_Flop d_ff_1 (.clk(Save), .D(A[0]), .Q(out_4[0]), .reset(Reset));  // open: Qn, preset, en
  D_Flip_Flop d_ff_2 (.clk(Save), .D(A[1]), .Q(out_4[1]), .reset(Reset));  // open: Qn, preset, en
  D_Flip_Flop d_ff_3 (.clk(Save), .D(A[2]), .Q(out_4[2]), .reset(Reset));  // open: Qn, preset, en
  D_Flip_Flop d_ff_4 (.clk(Save), .D(A[3]), .Q(out_4[3]), .reset(Reset));  // open: Qn, preset, en
  D_Flip_Flop d_ff_5 (.clk(Save), .D(A[4]), .Q(out_4[4]), .reset(Reset));  // open: Qn, preset, en
  D_Flip_Flop d_ff_6 (.clk(Save), .D(A[5]), .Q(out_4[5]), .reset(Reset));  // open: Qn, preset, en
  D_Flip_Flop d_ff_7 (.clk(Save), .D(A[6]), .Q(out_4[6]), .reset(Reset));  // open: Qn, preset, en
  D_Flip_Flop d_ff_8 (.clk(Save), .D(A[7]), .Q(out_4[7]), .reset(Reset));  // open: Qn, preset, en
  D_Flip_Flop d_ff_9 (.clk(Save), .D(A[8]), .Q(out_4[8]), .reset(Reset));  // open: Qn, preset, en
  D_Flip_Flop d_ff_10 (.clk(Save), .D(A[9]), .Q(out_4[9]), .reset(Reset));  // open: Qn, preset, en
  D_Flip_Flop d_ff_11 (.clk(Save), .D(A[10]), .Q(out_4[10]), .reset(Reset));  // open: Qn, preset, en
  D_Flip_Flop d_ff_12 (.clk(Save), .D(A[11]), .Q(out_4[11]), .reset(Reset));  // open: Qn, preset, en
  D_Flip_Flop d_ff_13 (.clk(Save), .D(A[12]), .Q(out_4[12]), .reset(Reset));  // open: Qn, preset, en
  D_Flip_Flop d_ff_14 (.clk(Save), .D(A[13]), .Q(out_4[13]), .reset(Reset));  // open: Qn, preset, en
  D_Flip_Flop d_ff_15 (.clk(Save), .D(A[14]), .Q(out_4[14]), .reset(Reset));  // open: Qn, preset, en
  D_Flip_Flop d_ff_16 (.clk(Save), .D(A[15]), .Q(out_4[15]), .reset(Reset));  // open: Qn, preset, en
  D_Flip_Flop d_ff_17 (.clk(Save), .D(A[16]), .Q(out_4[16]), .reset(Reset));  // open: Qn, preset, en
  D_Flip_Flop d_ff_18 (.clk(Save), .D(A[17]), .Q(out_4[17]), .reset(Reset));  // open: Qn, preset, en
  D_Flip_Flop d_ff_19 (.clk(Save), .D(A[18]), .Q(out_4[18]), .reset(Reset));  // open: Qn, preset, en
  D_Flip_Flop d_ff_20 (.clk(Save), .D(A[19]), .Q(out_4[19]), .reset(Reset));  // open: Qn, preset, en
  D_Flip_Flop d_ff_21 (.clk(Save), .D(A[20]), .Q(out_4[20]), .reset(Reset));  // open: Qn, preset, en
  D_Flip_Flop d_ff_22 (.clk(Save), .D(A[21]), .Q(out_4[21]), .reset(Reset));  // open: Qn, preset, en
  D_Flip_Flop d_ff_23 (.clk(Save), .D(A[22]), .Q(out_4[22]), .reset(Reset));  // open: Qn, preset, en
  D_Flip_Flop d_ff_24 (.clk(Save), .D(A[23]), .Q(out_4[23]), .reset(Reset));  // open: Qn, preset, en
  D_Flip_Flop d_ff_25 (.clk(Save), .D(A[24]), .Q(out_4[24]), .reset(Reset));  // open: Qn, preset, en
  D_Flip_Flop d_ff_26 (.clk(Save), .D(A[25]), .Q(out_4[25]), .reset(Reset));  // open: Qn, preset, en
  D_Flip_Flop d_ff_27 (.clk(Save), .D(A[26]), .Q(out_4[26]), .reset(Reset));  // open: Qn, preset, en
  D_Flip_Flop d_ff_28 (.clk(Save), .D(A[27]), .Q(out_4[27]), .reset(Reset));  // open: Qn, preset, en
  D_Flip_Flop d_ff_29 (.clk(Save), .D(A[28]), .Q(out_4[28]), .reset(Reset));  // open: Qn, preset, en
  D_Flip_Flop d_ff_30 (.clk(Save), .D(A[29]), .Q(out_4[29]), .reset(Reset));  // open: Qn, preset, en
  D_Flip_Flop d_ff_31 (.clk(Save), .D(A[30]), .Q(out_4[30]), .reset(Reset));  // open: Qn, preset, en
  D_Flip_Flop d_ff_32 (.clk(Save), .D(A[31]), .Q(out_4[31]), .reset(Reset));  // open: Qn, preset, en
endmodule

module BancoRegistrador (
  input  [31:0] in_1,
  input  Reset,
  input  Save,
  input  [4:0] ViewASelec,
  input  [4:0] RegSelect,
  input  [4:0] ViewBSelec,
  output [31:0] ViewASelect,
  output [31:0] ViewBSelect
);

  wire demultiplexer_1_out0, demultiplexer_1_out1, demultiplexer_1_out2, demultiplexer_1_out3,
       demultiplexer_1_out4, demultiplexer_1_out5, demultiplexer_1_out6, demultiplexer_1_out7,
       demultiplexer_1_out8, demultiplexer_1_out9, demultiplexer_1_out10, demultiplexer_1_out11,
       demultiplexer_1_out12, demultiplexer_1_out13, demultiplexer_1_out14, demultiplexer_1_out15,
       demultiplexer_1_out16, demultiplexer_1_out17, demultiplexer_1_out18, demultiplexer_1_out19,
       demultiplexer_1_out20, demultiplexer_1_out21, demultiplexer_1_out22, demultiplexer_1_out23,
       demultiplexer_1_out24, demultiplexer_1_out25, demultiplexer_1_out26, demultiplexer_1_out27,
       demultiplexer_1_out28, demultiplexer_1_out29, demultiplexer_1_out30, demultiplexer_1_out31;
  wire [31:0] flip_flop_1_out_4, flip_flop_2_out_4, flip_flop_3_out_4, flip_flop_4_out_4, flip_flop_5_out_4,
       flip_flop_6_out_4, flip_flop_7_out_4, flip_flop_8_out_4, flip_flop_9_out_4, flip_flop_10_out_4,
       flip_flop_11_out_4, flip_flop_12_out_4, flip_flop_13_out_4, flip_flop_14_out_4, flip_flop_15_out_4,
       flip_flop_16_out_4, flip_flop_17_out_4, flip_flop_18_out_4, flip_flop_19_out_4, flip_flop_20_out_4,
       flip_flop_21_out_4, flip_flop_22_out_4, flip_flop_23_out_4, flip_flop_24_out_4, flip_flop_25_out_4,
       flip_flop_26_out_4, flip_flop_27_out_4, flip_flop_28_out_4, flip_flop_29_out_4, flip_flop_30_out_4,
       flip_flop_31_out_4, flip_flop_32_out_4;

  Demultiplexer #(.select(5), .enable("false")) demultiplexer_1 (
    .out0(demultiplexer_1_out0), .out1(demultiplexer_1_out1), .out2(demultiplexer_1_out2),
    .out3(demultiplexer_1_out3), .out4(demultiplexer_1_out4), .out5(demultiplexer_1_out5),
    .out6(demultiplexer_1_out6), .out7(demultiplexer_1_out7), .out8(demultiplexer_1_out8),
    .out9(demultiplexer_1_out9), .out10(demultiplexer_1_out10), .out11(demultiplexer_1_out11),
    .out12(demultiplexer_1_out12), .out13(demultiplexer_1_out13), .out14(demultiplexer_1_out14),
    .out15(demultiplexer_1_out15), .out16(demultiplexer_1_out16), .out17(demultiplexer_1_out17),
    .out18(demultiplexer_1_out18), .out19(demultiplexer_1_out19), .out20(demultiplexer_1_out20),
    .out21(demultiplexer_1_out21), .out22(demultiplexer_1_out22), .out23(demultiplexer_1_out23),
    .out24(demultiplexer_1_out24), .out25(demultiplexer_1_out25), .out26(demultiplexer_1_out26),
    .out27(demultiplexer_1_out27), .out28(demultiplexer_1_out28), .out29(demultiplexer_1_out29),
    .out30(demultiplexer_1_out30), .out31(demultiplexer_1_out31), .in(Save), .sel(RegSelect));
  flip_flop flip_flop_1 (.A(in_1), .Save(demultiplexer_1_out0), .Reset(Reset), .out_4(flip_flop_1_out_4));
  flip_flop flip_flop_2 (
    .A(in_1), .Save(demultiplexer_1_out1), .Reset(demultiplexer_1_out0), .out_4(flip_flop_2_out_4));
  flip_flop flip_flop_3 (
    .A(in_1), .Save(demultiplexer_1_out2), .Reset(demultiplexer_1_out0), .out_4(flip_flop_3_out_4));
  flip_flop flip_flop_4 (
    .A(in_1), .Save(demultiplexer_1_out3), .Reset(demultiplexer_1_out0), .out_4(flip_flop_4_out_4));
  flip_flop flip_flop_5 (
    .A(in_1), .Save(demultiplexer_1_out4), .Reset(demultiplexer_1_out0), .out_4(flip_flop_5_out_4));
  flip_flop flip_flop_6 (
    .A(in_1), .Save(demultiplexer_1_out5), .Reset(demultiplexer_1_out0), .out_4(flip_flop_6_out_4));
  flip_flop flip_flop_7 (
    .A(in_1), .Save(demultiplexer_1_out6), .Reset(demultiplexer_1_out0), .out_4(flip_flop_7_out_4));
  flip_flop flip_flop_8 (
    .A(in_1), .Save(demultiplexer_1_out7), .Reset(demultiplexer_1_out0), .out_4(flip_flop_8_out_4));
  flip_flop flip_flop_9 (
    .A(in_1), .Save(demultiplexer_1_out8), .Reset(demultiplexer_1_out0), .out_4(flip_flop_9_out_4));
  flip_flop flip_flop_10 (
    .A(in_1), .Save(demultiplexer_1_out9), .Reset(demultiplexer_1_out0), .out_4(flip_flop_10_out_4));
  flip_flop flip_flop_11 (
    .A(in_1), .Save(demultiplexer_1_out10), .Reset(demultiplexer_1_out0), .out_4(flip_flop_11_out_4));
  flip_flop flip_flop_12 (
    .A(in_1), .Save(demultiplexer_1_out11), .Reset(demultiplexer_1_out0), .out_4(flip_flop_12_out_4));
  flip_flop flip_flop_13 (
    .A(in_1), .Save(demultiplexer_1_out12), .Reset(demultiplexer_1_out0), .out_4(flip_flop_13_out_4));
  flip_flop flip_flop_14 (
    .A(in_1), .Save(demultiplexer_1_out13), .Reset(demultiplexer_1_out0), .out_4(flip_flop_14_out_4));
  flip_flop flip_flop_15 (
    .A(in_1), .Save(demultiplexer_1_out14), .Reset(demultiplexer_1_out0), .out_4(flip_flop_15_out_4));
  flip_flop flip_flop_16 (
    .A(in_1), .Save(demultiplexer_1_out15), .Reset(demultiplexer_1_out0), .out_4(flip_flop_16_out_4));
  flip_flop flip_flop_17 (
    .A(in_1), .Save(demultiplexer_1_out16), .Reset(demultiplexer_1_out0), .out_4(flip_flop_17_out_4));
  flip_flop flip_flop_18 (
    .A(in_1), .Save(demultiplexer_1_out17), .Reset(demultiplexer_1_out0), .out_4(flip_flop_18_out_4));
  flip_flop flip_flop_19 (
    .A(in_1), .Save(demultiplexer_1_out18), .Reset(demultiplexer_1_out0), .out_4(flip_flop_19_out_4));
  flip_flop flip_flop_20 (
    .A(in_1), .Save(demultiplexer_1_out19), .Reset(demultiplexer_1_out0), .out_4(flip_flop_20_out_4));
  flip_flop flip_flop_21 (
    .A(in_1), .Save(demultiplexer_1_out20), .Reset(demultiplexer_1_out0), .out_4(flip_flop_21_out_4));
  flip_flop flip_flop_22 (
    .A(in_1), .Save(demultiplexer_1_out21), .Reset(demultiplexer_1_out0), .out_4(flip_flop_22_out_4));
  flip_flop flip_flop_23 (
    .A(in_1), .Save(demultiplexer_1_out22), .Reset(demultiplexer_1_out0), .out_4(flip_flop_23_out_4));
  flip_flop flip_flop_24 (
    .A(in_1), .Save(demultiplexer_1_out23), .Reset(demultiplexer_1_out0), .out_4(flip_flop_24_out_4));
  flip_flop flip_flop_25 (
    .A(in_1), .Save(demultiplexer_1_out24), .Reset(demultiplexer_1_out0), .out_4(flip_flop_25_out_4));
  flip_flop flip_flop_26 (
    .A(in_1), .Save(demultiplexer_1_out25), .Reset(demultiplexer_1_out0), .out_4(flip_flop_26_out_4));
  flip_flop flip_flop_27 (
    .A(in_1), .Save(demultiplexer_1_out26), .Reset(demultiplexer_1_out0), .out_4(flip_flop_27_out_4));
  flip_flop flip_flop_28 (
    .A(in_1), .Save(demultiplexer_1_out27), .Reset(demultiplexer_1_out0), .out_4(flip_flop_28_out_4));
  flip_flop flip_flop_29 (
    .A(in_1), .Save(demultiplexer_1_out28), .Reset(demultiplexer_1_out0), .out_4(flip_flop_29_out_4));
  flip_flop flip_flop_30 (
    .A(in_1), .Save(demultiplexer_1_out29), .Reset(demultiplexer_1_out0), .out_4(flip_flop_30_out_4));
  flip_flop flip_flop_31 (
    .A(in_1), .Save(demultiplexer_1_out30), .Reset(demultiplexer_1_out0), .out_4(flip_flop_31_out_4));
  flip_flop flip_flop_32 (
    .A(in_1), .Save(demultiplexer_1_out31), .Reset(demultiplexer_1_out0), .out_4(flip_flop_32_out_4));
  Multiplexer #(.select(5), .width(32), .enable("false")) multiplexer_1 (
    .in0(flip_flop_1_out_4), .in1(flip_flop_2_out_4), .in2(flip_flop_3_out_4), .in3(flip_flop_4_out_4),
    .in4(flip_flop_5_out_4), .in5(flip_flop_6_out_4), .in6(flip_flop_7_out_4), .in7(flip_flop_8_out_4),
    .in8(flip_flop_9_out_4), .in9(flip_flop_10_out_4), .in10(flip_flop_11_out_4), .in11(flip_flop_12_out_4),
    .in12(flip_flop_13_out_4), .in13(flip_flop_14_out_4), .in14(flip_flop_15_out_4),
    .in15(flip_flop_16_out_4), .in16(flip_flop_17_out_4), .in17(flip_flop_18_out_4),
    .in18(flip_flop_19_out_4), .in19(flip_flop_20_out_4), .in20(flip_flop_21_out_4),
    .in21(flip_flop_22_out_4), .in22(flip_flop_23_out_4), .in23(flip_flop_24_out_4),
    .in24(flip_flop_25_out_4), .in25(flip_flop_26_out_4), .in26(flip_flop_27_out_4),
    .in27(flip_flop_28_out_4), .in28(flip_flop_29_out_4), .in29(flip_flop_30_out_4),
    .in30(flip_flop_31_out_4), .in31(flip_flop_32_out_4), .out(ViewASelect), .sel(ViewASelec));
  Multiplexer #(.select(5), .width(32), .enable("false")) multiplexer_2 (
    .in0(flip_flop_1_out_4), .in1(flip_flop_2_out_4), .in2(flip_flop_3_out_4), .in3(flip_flop_4_out_4),
    .in4(flip_flop_5_out_4), .in5(flip_flop_6_out_4), .in6(flip_flop_7_out_4), .in7(flip_flop_8_out_4),
    .in8(flip_flop_9_out_4), .in9(flip_flop_10_out_4), .in10(flip_flop_11_out_4), .in11(flip_flop_12_out_4),
    .in12(flip_flop_13_out_4), .in13(flip_flop_14_out_4), .in14(flip_flop_15_out_4),
    .in15(flip_flop_16_out_4), .in16(flip_flop_17_out_4), .in17(flip_flop_18_out_4),
    .in18(flip_flop_19_out_4), .in19(flip_flop_20_out_4), .in20(flip_flop_21_out_4),
    .in21(flip_flop_22_out_4), .in22(flip_flop_23_out_4), .in23(flip_flop_24_out_4),
    .in24(flip_flop_25_out_4), .in25(flip_flop_26_out_4), .in26(flip_flop_27_out_4),
    .in27(flip_flop_28_out_4), .in28(flip_flop_29_out_4), .in29(flip_flop_30_out_4),
    .in30(flip_flop_31_out_4), .in31(flip_flop_32_out_4), .out(ViewBSelect), .sel(ViewBSelec));
endmodule

module test (
  input  in_1,
  input  in_2,
  input  in_3,
  input  in_4,
  input  in_5
);

  D_Flip_Flop d_ff_1 (.clk(in_5), .D(in_1));  // open: Q, Qn, preset, en, reset
  D_Flip_Flop d_ff_2 (.clk(in_5), .D(in_2));  // open: Q, Qn, preset, en, reset
  D_Flip_Flop d_ff_3 (.clk(in_5), .D(in_3));  // open: Q, Qn, preset, en, reset
  D_Flip_Flop d_ff_4 (.clk(in_5), .D(in_4));  // open: Q, Qn, preset, en, reset
endmodule
