// Logisim project mux.circ as structural Verilog: 5 circuits, main circuit mux2
module mux2 (
  input  I0,
  input  I1,
  input  Sel,
  output out_4
);

  wire and_1_out, and_2_out;

  and and_1 (and_1_out, I0, ~Sel);  // AND_Gate
  and and_2 (and_2_out, I1, Sel);
  or or_1 (out_4, and_1_out, and_2_out);
endmodule

module mux4 (
  input  l0,
  input  l1,
  input  l2,
  input  l3,
  input  sel1,
  input  sel0,
  output out_7
);

  wire mux2_1_out_4, mux2_2_out_4;

  mux2 mux2_1 (.I0(l0), .I1(l1), .Sel(sel0), .out_4(mux2_1_out_4));
  mux2 mux2_2 (.I0(l2), .I1(l3), .Sel(sel0), .out_4(mux2_2_out_4));
  mux2 mux2_3 (.I0(mux2_1_out_4), .I1(mux2_2_out_4), .Sel(sel1), .out_4(out_7));
endmodule

module mux8 (
  input  l0,
  input  l1,
  input  l2,
  input  l3,
  input  l4,
  input  l5,
  input  l6,
  input  l7,
  input  sel2,
  input  sel1,
  input  sel0,
  output out_12
);

  wire mux4_1_out_7, mux4_2_out_7;

  mux4 mux4_1 (.l0(l0), .l1(l1), .l2(l2), .l3(l3), .sel1(sel1), .sel0(sel0), .out_7(mux4_1_out_7));
  mux4 mux4_2 (.l0(l4), .l1(l5), .l2(l6), .l3(l7), .sel1(sel1), .sel0(sel0), .out_7(mux4_2_out_7));
  mux2 mux2_1 (.I0(mux4_1_out_7), .I1(mux4_2_out_7), .Sel(sel2), .out_4(out_12));
endmodule

module mux16 (
  input  l0,
  input  l1,
  input  l2,
  input  l3,
  input  l4,
  input  l5,
  input  l6,
  input  l7,
  input  l8,
  input  l9,
  input  l10,
  input  l11,
  input  l12,
  input  l13,
  input  l14,
  input  l15,
  input  sel3,
  input  sel2,
  input  sel1,
  input  sel0,
  output out_21
);

  wire mux8_1_out_12, mux8_2_out_12;

  mux8 mux8_1 (
    .l0(l0), .l1(l1), .l2(l2), .l3(l3), .l4(l4), .l5(l5), .l6(l6), .l7(l7), .sel2(sel2), .sel1(sel1),
    .sel0(sel0), .out_12(mux8_1_out_12));
  mux8 mux8_2 (
    .l0(l8), .l1(l9), .l2(l10), .l3(l11), .l4(l12), .l5(l13), .l6(l14), .l7(l15), .sel2(sel2), .sel1(sel1),
    .sel0(sel0), .out_12(mux8_2_out_12));
  mux2 mux2_1 (.I0(mux8_1_out_12), .I1(mux8_2_out_12), .Sel(sel3), .out_4(out_21));
endmodule

module mux32 (
  input  l0,
  input  l1,
  input  l2,
  input  l3,
  input  l4,
  input  l5,
  input  l6,
  input  l7,
  input  l8,
  input  l9,
  input  l10,
  input  l11,
  input  l12,
  input  l13,
  input  l14,
  input  l15,
  input  l16,
  input  l17,
  input  l18,
  input  l19,
  input  l20,
  input  l21,
  input  l22,
  input  l23,
  input  l24,
  input  l25,
  input  l26,
  input  l27,
  input  l28,
  input  l29,
  input  l30,
  input  sel5,
  input  sel3,
  input  sel2,
  input  sel1,
  input  sel0,
  input  l31,
  output out_38
);

  wire mux16_1_out_21, mux16_2_out_21;

  mux16 mux16_1 (
    .l0(l0), .l1(l1), .l2(l2), .l3(l3), .l4(l4), .l5(l5), .l6(l6), .l7(l7), .l8(l8), .l9(l9), .l10(l10),
    .l11(l11), .l12(l12), .l13(l13), .l14(l14), .l15(l15), .sel3(sel3), .sel2(sel2), .sel1(sel1),
    .sel0(sel0), .out_21(mux16_1_out_21));
  mux16 mux16_2 (
    .l0(l16), .l1(l17), .l2(l18), .l3(l19), .l4(l20), .l5(l21), .l6(l22), .l7(l23), .l8(l24), .l9(l25),
    .l10(l26), .l11(l27), .l12(l28), .l13(l29), .l14(l30), .l15(l31), .sel3(sel3), .sel2(sel2), .sel1(sel1),
    .sel0(sel0), .out_21(mux16_2_out_21));
  mux2 mux2_1 (.I0(mux16_1_out_21), .I1(mux16_2_out_21), .Sel(sel5), .out_4(out_38));
endmodule
